// Logisim project ax8.circ as structural Verilog: 14 circuits, main circuit full_adder
module main (
);

  wire adder_subtractor_1_cout, adder_subtractor_1_overflow, clock_1_out, clock_2_out, clock_3_out,
       d_flipflop_1_nq, d_flipflop_1_q, d_latch_1_nq, d_latch_1_q, dipswitch_4_p1, dipswitch_5_p1,
       dipswitch_10_p1, dipswitch_11_p1, dipswitch_12_p1, dipswitch_13_p1, dipswitch_15_p1, dipswitch_16_p1,
       dipswitch_17_p1, dipswitch_19_p1, dipswitch_21_p1, dipswitch_22_p1, dipswitch_23_p1, dipswitch_24_p1,
       dipswitch_24_p2, dipswitch_25_p1, dipswitch_29_p1, full_adder_1_cout, full_adder_1_y,
       multiplier_4_1_overflow, mux_2to1_1_y, ripple_adder_4_1_cout, ripple_adder_8_1_c6,
       ripple_adder_8_1_cout, shifter_8_1_cout;
  wire [3:0] adder_subtractor_1_y, adder_subtractor_1_y_2, demux_2to4_1_y, multiplier_4_1_y,
       multiplier_4_1_y_2, register_8_1_q, register_8_1_q_2, ripple_adder_4_1_y, ripple_adder_8_1_y,
       ripple_adder_8_1_y_2, undriven_3, undriven_4, undriven_5, undriven_8;
  wire [7:0] demux_3to8_1_y, shifter_8_1_y, undriven, undriven_2, undriven_6, undriven_7, undriven_9,
       undriven_10;

  // DipSwitch #(.number(4)) dipswitch_1: pin names not known
  // DipSwitch dipswitch_2: pin names not known
  // DipSwitch dipswitch_3: pin names not known
  // DipSwitch #(.number(1)) dipswitch_4: pin names not known; wires that end beside it: dipswitch_4_p1
  // DipSwitch #(.number(1)) dipswitch_5: pin names not known; wires that end beside it: dipswitch_5_p1
  // DipSwitch #(.number(4)) dipswitch_6: pin names not known
  // DipSwitch dipswitch_7: pin names not known
  // DipSwitch dipswitch_8: pin names not known
  // DipSwitch #(.number(4)) dipswitch_9: pin names not known
  // DipSwitch #(.number(1)) dipswitch_10: pin names not known; wires that end beside it: dipswitch_10_p1
  // DipSwitch #(.number(1)) dipswitch_11: pin names not known; wires that end beside it: dipswitch_11_p1
  // DipSwitch #(.number(1)) dipswitch_12: pin names not known; wires that end beside it: dipswitch_12_p1
  // DipSwitch #(.number(1)) dipswitch_13: pin names not known; wires that end beside it: dipswitch_13_p1
  // DipSwitch #(.number(4)) dipswitch_14: pin names not known
  LED led_1 (.in(full_adder_1_y));
  full_adder full_adder_1 (
    .A(dipswitch_4_p1), .B(dipswitch_5_p1), .Cin(dipswitch_10_p1), .Y(full_adder_1_y),
    .Cout(full_adder_1_cout));
  LED led_2 (.in(full_adder_1_cout));
  Hex_Digit_Display #(.decimalPoint("false")) hex_digit_display_1 (.value(ripple_adder_4_1_y));
  ripple_adder_4 ripple_adder_4_1 (
    .A(undriven_3), .B(undriven_5), .Cin(dipswitch_11_p1), .Y(ripple_adder_4_1_y),
    .Cout(ripple_adder_4_1_cout));
  LED led_3 (.in(ripple_adder_4_1_cout));
  Hex_Digit_Display #(.decimalPoint("false")) hex_digit_display_2 (.value(ripple_adder_8_1_y));
  ripple_adder_8 ripple_adder_8_1 (
    .A(undriven_2), .B(undriven_7), .Cin(dipswitch_12_p1), .Y({ripple_adder_8_1_y, ripple_adder_8_1_y_2}),
    .Cout(ripple_adder_8_1_cout), .C6(ripple_adder_8_1_c6));
  LED led_4 (.in(ripple_adder_8_1_c6));
  LED led_5 (.in(ripple_adder_8_1_cout));
  Hex_Digit_Display #(.decimalPoint("false")) hex_digit_display_3 (.value(adder_subtractor_1_y));
  // DipSwitch #(.number(1)) dipswitch_15: pin names not known; wires that end beside it: dipswitch_15_p1
  adder_subtractor adder_subtractor_1 (
    .M(dipswitch_15_p1), .B(undriven_6), .A(undriven), .Cin(dipswitch_13_p1),
    .Y({adder_subtractor_1_y, adder_subtractor_1_y_2}), .Cout(adder_subtractor_1_cout),
    .Overflow(adder_subtractor_1_overflow));
  LED led_6 (.in(adder_subtractor_1_overflow));
  LED led_7 (.in(adder_subtractor_1_cout));
  Hex_Digit_Display #(.decimalPoint("false")) hex_digit_display_4 (.value(multiplier_4_1_y));
  multiplier_4 multiplier_4_1 (
    .B(undriven_4), .A(undriven_8), .Y({multiplier_4_1_y, multiplier_4_1_y_2}),
    .Overflow(multiplier_4_1_overflow));
  LED led_8 (.in(multiplier_4_1_overflow));
  Hex_Digit_Display #(.decimalPoint("false")) hex_digit_display_5 (.value(ripple_adder_8_1_y_2));
  Hex_Digit_Display #(.decimalPoint("false")) hex_digit_display_6 (.value(adder_subtractor_1_y_2));
  Hex_Digit_Display #(.decimalPoint("false")) hex_digit_display_7 (.value(multiplier_4_1_y_2));
  Clock clock_1 (.out(clock_1_out));
  // DipSwitch #(.number(1)) dipswitch_16: pin names not known; wires that end beside it: dipswitch_16_p1
  Clock clock_2 (.out(clock_2_out));
  // DipSwitch #(.number(1)) dipswitch_17: pin names not known; wires that end beside it: dipswitch_17_p1
  // DipSwitch dipswitch_18: pin names not known
  Clock clock_3 (.out(clock_3_out));
  // DipSwitch #(.number(1)) dipswitch_19: pin names not known; wires that end beside it: dipswitch_19_p1
  LED led_9 (.in(d_latch_1_q));
  d_latch d_latch_1 (.D(dipswitch_16_p1), .CLK(clock_1_out), .Q(d_latch_1_q), .NQ(d_latch_1_nq));
  LED led_10 (.in(d_latch_1_nq));
  LED led_11 (.in(d_flipflop_1_q));
  d_flipflop d_flipflop_1 (.D(dipswitch_17_p1), .CLK(clock_2_out), .Q(d_flipflop_1_q), .NQ(d_flipflop_1_nq));
  LED led_12 (.in(d_flipflop_1_nq));
  Hex_Digit_Display #(.decimalPoint("false")) hex_digit_display_8 (.value(register_8_1_q_2));
  Hex_Digit_Display #(.decimalPoint("false")) hex_digit_display_9 (.value(register_8_1_q));
  register_8 register_8_1 (
    .CLK(clock_3_out), .WE(dipswitch_19_p1), .D(undriven_9), .Q({register_8_1_q_2, register_8_1_q}));
  // DipSwitch dipswitch_20: pin names not known
  // DipSwitch #(.number(1)) dipswitch_21: pin names not known; wires that end beside it: dipswitch_21_p1
  // DipSwitch #(.number(1)) dipswitch_22: pin names not known; wires that end beside it: dipswitch_22_p1
  LED led_13 (.in(shifter_8_1_cout));
  LED led_14 (.in(shifter_8_1_y[0]));
  LED led_15 (.in(shifter_8_1_y[1]));
  LED led_16 (.in(shifter_8_1_y[2]));
  shifter_8 shifter_8_1 (
    .A(undriven_10), .Cin(dipswitch_22_p1), .M(dipswitch_21_p1), .Y(shifter_8_1_y), .Cout(shifter_8_1_cout));
  LED led_17 (.in(shifter_8_1_y[3]));
  LED led_18 (.in(shifter_8_1_y[4]));
  LED led_19 (.in(shifter_8_1_y[5]));
  LED led_20 (.in(shifter_8_1_y[6]));
  LED led_21 (.in(shifter_8_1_y[7]));
  LED led_22 (.in(shifter_8_1_cout));
  // DipSwitch #(.number(1)) dipswitch_23: pin names not known; wires that end beside it: dipswitch_23_p1
  // DipSwitch #(.number(1)) dipswitch_24: pin names not known; wires that end beside it: dipswitch_24_p1, dipswitch_24_p2
  // DipSwitch #(.number(1)) dipswitch_25: pin names not known; wires that end beside it: dipswitch_25_p1
  // DipSwitch #(.number(1)) dipswitch_26: pin names not known
  // DipSwitch #(.number(1)) dipswitch_27: pin names not known
  LED led_23 (.in(mux_2to1_1_y));
  mux_2to1 mux_2to1_1 (.A(dipswitch_24_p2), .B(dipswitch_24_p1), .S(dipswitch_23_p1), .Y(mux_2to1_1_y));
  // DipSwitch #(.number(1)) dipswitch_28: pin names not known
  LED led_24 (.in(demux_2to4_1_y[3]));
  LED led_25 (.in(demux_2to4_1_y[2]));
  LED led_26 (.in(demux_2to4_1_y[1]));
  demux_2to4 demux_2to4_1 (.E(dipswitch_25_p1), .Y(demux_2to4_1_y));  // open: S1, S0
  LED led_27 (.in(demux_2to4_1_y[0]));
  LED led_28 (.in(demux_3to8_1_y[7]));
  LED led_29 (.in(demux_3to8_1_y[6]));
  LED led_30 (.in(demux_3to8_1_y[5]));
  // DipSwitch #(.number(1)) dipswitch_29: pin names not known; wires that end beside it: dipswitch_29_p1
  // DipSwitch #(.number(1)) dipswitch_30: pin names not known
  // DipSwitch #(.number(1)) dipswitch_31: pin names not known
  LED led_31 (.in(demux_3to8_1_y[4]));
  LED led_32 (.in(demux_3to8_1_y[3]));
  LED led_33 (.in(demux_3to8_1_y[2]));
  LED led_34 (.in(demux_3to8_1_y[1]));
  // DipSwitch #(.number(1)) dipswitch_32: pin names not known
  demux_3to8 demux_3to8_1 (.E(dipswitch_29_p1), .Y(demux_3to8_1_y));  // open: S0, S1, S2
  LED led_35 (.in(demux_3to8_1_y[0]));

  // Notes on the sheet:
  //   Test: Full Adder
  //   Test: Ripple Adder with 4-bits
  //   Test: Ripple Adder with 8-bits
  //   Test: Adder-Subtractor with 8-bits
  //   Test: Multiplier with 4-bits
  //   Test: D-Latch
  //   Test: D Flip Flop
  //   Test: Register of 8-bits
  //   Test: Multiplexer 2 to 1
  //   Test: Shifter with 8-bits
endmodule

module d_latch (
  input  D,
  input  CLK,
  output Q,
  output NQ
);

  wire nand_1_out, nand_2_out, not_1_out;

  not not_1 (not_1_out, D);
  nand nand_1 (nand_1_out, D, CLK);
  nand nand_2 (nand_2_out, CLK, not_1_out);
  nand nand_3 (Q, NQ, nand_1_out);
  nand nand_4 (NQ, nand_2_out, Q);
endmodule

module d_flipflop (
  input  D,
  input  CLK,
  output Q,
  output NQ
);

  wire Master_q, not_1_out;

  not not_1 (not_1_out, CLK);
  d_latch Master (.D(D), .CLK(not_1_out), .Q(Master_q));  // open: NQ
  d_latch Slave (.D(Master_q), .CLK(CLK), .Q(Q), .NQ(NQ));

  // Notes on the sheet:
  //   Rising edge D-FlipFlop
endmodule

module mux_2to1 (
  input  S,
  input  A,
  input  B,
  output Y
);

  wire nand_1_out, nand_3_out, not_1_out;

  not not_1 (not_1_out, S);
  nand nand_1 (nand_1_out, not_1_out, A);
  nand nand_2 (Y, nand_1_out, nand_3_out);
  nand nand_3 (nand_3_out, B, S);
endmodule

module demux_2to4 (
  input  S1,
  input  S0,
  input  E,
  output [3:0] Y
);

  wire not_1_out, not_2_out;

  not not_1 (not_1_out, S1);
  not not_2 (not_2_out, S0);
  and and_1 (Y[0], not_2_out, E, not_1_out);
  and and_2 (Y[1], S0, E, not_1_out);
  and and_3 (Y[2], not_2_out, E, S1);
  and and_4 (Y[3], S0, E, S1);
endmodule

module demux_3to8 (
  input  S0,
  input  S1,
  input  S2,
  input  E,
  output [7:0] Y
);

  wire and_1_out, and_2_out;

  and and_1 (and_1_out, ~S2, E);  // AND_Gate
  and and_2 (and_2_out, S2, E);
  demux_2to4 demux_2to4_1 (.S1(S1), .S0(S0), .E(and_1_out), .Y(Y[3:0]));
  demux_2to4 demux_2to4_2 (.S1(S1), .S0(S0), .E(and_2_out), .Y(Y[7:4]));
endmodule

module demux_4to16 (
  input  S0,
  input  S1,
  input  S2,
  input  S3,
  input  E,
  output [15:0] Y
);

  wire and_1_out, and_2_out;

  and and_1 (and_1_out, ~S3, E);  // AND_Gate
  and and_2 (and_2_out, S3, E);
  demux_3to8 demux_3to8_1 (.S0(S0), .S1(S1), .S2(S2), .E(and_1_out), .Y(Y[7:0]));
  demux_3to8 demux_3to8_2 (.S0(S0), .S1(S1), .S2(S2), .E(and_2_out), .Y(Y[15:8]));
endmodule

module full_adder (
  input  A,
  input  B,
  input  Cin,
  output Y,
  output Cout
);

  wire and_1_out, and_2_out, xor_1_out;

  xor xor_1 (xor_1_out, A, B);
  and and_1 (and_1_out, xor_1_out, Cin);
  and and_2 (and_2_out, A, B);
  xor xor_2 (Y, xor_1_out, Cin);
  or or_1 (Cout, and_1_out, and_2_out);
endmodule

module ripple_adder_4 (
  input  [3:0] A,
  input  [3:0] B,
  input  Cin,
  output [3:0] Y,
  output Cout
);

  wire full_adder_1_cout, full_adder_2_cout, full_adder_3_cout;

  full_adder full_adder_1 (.A(A[0]), .B(B[0]), .Cin(Cin), .Y(Y[0]), .Cout(full_adder_1_cout));
  full_adder full_adder_2 (.A(A[1]), .B(B[1]), .Cin(full_adder_1_cout), .Y(Y[1]), .Cout(full_adder_2_cout));
  full_adder full_adder_3 (.A(A[2]), .B(B[2]), .Cin(full_adder_2_cout), .Y(Y[2]), .Cout(full_adder_3_cout));
  full_adder full_adder_4 (.A(A[3]), .B(B[3]), .Cin(full_adder_3_cout), .Y(Y[3]), .Cout(Cout));
endmodule

module ripple_adder_8 (
  input  [7:0] A,
  input  [7:0] B,
  input  Cin,
  output [7:0] Y,
  output Cout,
  output C6
);

  wire full_adder_1_cout, full_adder_2_cout, full_adder_3_cout, full_adder_4_cout, full_adder_5_cout,
       full_adder_6_cout;

  full_adder full_adder_1 (.A(A[0]), .B(B[0]), .Cin(Cin), .Y(Y[0]), .Cout(full_adder_1_cout));
  full_adder full_adder_2 (.A(A[1]), .B(B[1]), .Cin(full_adder_1_cout), .Y(Y[1]), .Cout(full_adder_2_cout));
  full_adder full_adder_3 (.A(A[2]), .B(B[2]), .Cin(full_adder_2_cout), .Y(Y[2]), .Cout(full_adder_3_cout));
  full_adder full_adder_4 (.A(A[3]), .B(B[3]), .Cin(full_adder_3_cout), .Y(Y[3]), .Cout(full_adder_4_cout));
  full_adder full_adder_5 (.A(A[4]), .B(B[4]), .Cin(full_adder_4_cout), .Y(Y[4]), .Cout(full_adder_5_cout));
  full_adder full_adder_6 (.A(A[5]), .B(B[5]), .Cin(full_adder_5_cout), .Y(Y[5]), .Cout(full_adder_6_cout));
  full_adder full_adder_7 (.A(A[6]), .B(B[6]), .Cin(full_adder_6_cout), .Y(Y[6]), .Cout(C6));
  full_adder full_adder_8 (.A(A[7]), .B(B[7]), .Cin(C6), .Y(Y[7]), .Cout(Cout));
endmodule

module register_8 (
  input  CLK,
  input  WE,
  input  [7:0] D,
  output [7:0] Q
);

  wire mux_2to1_1_p4, mux_2to1_2_p4, mux_2to1_3_p4, mux_2to1_4_p4, mux_2to1_5_p4, mux_2to1_6_p4,
       mux_2to1_7_p4, mux_2to1_8_p4;

  // mux_2to1 mux_2to1_1: pin names not known; wires that end beside it: Q[0], D[0], WE, mux_2to1_1_p4
  // mux_2to1 mux_2to1_2: pin names not known; wires that end beside it: Q[1], D[1], WE, mux_2to1_2_p4
  // mux_2to1 mux_2to1_3: pin names not known; wires that end beside it: Q[2], D[2], WE, mux_2to1_3_p4
  // mux_2to1 mux_2to1_4: pin names not known; wires that end beside it: Q[3], D[3], WE, mux_2to1_4_p4
  // mux_2to1 mux_2to1_5: pin names not known; wires that end beside it: Q[4], D[4], WE, mux_2to1_5_p4
  // mux_2to1 mux_2to1_6: pin names not known; wires that end beside it: Q[5], D[5], WE, mux_2to1_6_p4
  // mux_2to1 mux_2to1_7: pin names not known; wires that end beside it: Q[6], D[6], WE, mux_2to1_7_p4
  // mux_2to1 mux_2to1_8: pin names not known; wires that end beside it: Q[7], D[7], WE, mux_2to1_8_p4
  d_flipflop d_flipflop_1 (.D(mux_2to1_1_p4), .CLK(CLK), .Q(Q[0]));  // open: NQ
  d_flipflop d_flipflop_2 (.D(mux_2to1_2_p4), .CLK(CLK), .Q(Q[1]));  // open: NQ
  d_flipflop d_flipflop_3 (.D(mux_2to1_3_p4), .CLK(CLK), .Q(Q[2]));  // open: NQ
  d_flipflop d_flipflop_4 (.D(mux_2to1_4_p4), .CLK(CLK), .Q(Q[3]));  // open: NQ
  d_flipflop d_flipflop_5 (.D(mux_2to1_5_p4), .CLK(CLK), .Q(Q[4]));  // open: NQ
  d_flipflop d_flipflop_6 (.D(mux_2to1_6_p4), .CLK(CLK), .Q(Q[5]));  // open: NQ
  d_flipflop d_flipflop_7 (.D(mux_2to1_7_p4), .CLK(CLK), .Q(Q[6]));  // open: NQ
  d_flipflop d_flipflop_8 (.D(mux_2to1_8_p4), .CLK(CLK), .Q(Q[7]));  // open: NQ
endmodule

module adder_subtractor (
  input  M,
  input  Cin,
  input  [7:0] B,
  input  [7:0] A,
  output [7:0] Y,
  output Cout,
  output Overflow
);

  wire ripple_adder_8_1_c6;
  wire [7:0] xor_8_out;

  xor xor_1 (xor_8_out[7], M, B[7]);
  xor xor_2 (xor_8_out[6], M, B[6]);
  xor xor_3 (xor_8_out[5], M, B[5]);
  xor xor_4 (xor_8_out[4], M, B[4]);
  xor xor_5 (xor_8_out[3], M, B[3]);
  xor xor_6 (xor_8_out[2], M, B[2]);
  xor xor_7 (xor_8_out[1], M, B[1]);
  xor xor_8 (xor_8_out[0], M, B[0]);
  ripple_adder_8 ripple_adder_8_1 (.A(A), .B(xor_8_out), .Cin(Cin), .Y(Y), .Cout(Cout), .C6(ripple_adder_8_1_c6));
  xor xor_9 (Overflow, Cout, ripple_adder_8_1_c6);
endmodule

module shifter_8 (
  input  [7:0] A,
  input  Cin,
  input  M,
  output [7:0] Y,
  output Cout
);

  // mux_2to1 mux_2to1_1: pin names not known; wires that end beside it: A[4], Y[3], A[2], M
  // mux_2to1 mux_2to1_2: pin names not known; wires that end beside it: Cin, Y[7], A[6], M
  // mux_2to1 mux_2to1_3: pin names not known; wires that end beside it: A[3], Y[2], A[1], M
  // mux_2to1 mux_2to1_4: pin names not known; wires that end beside it: A[7], Y[6], A[5], M
  // mux_2to1 mux_2to1_5: pin names not known; wires that end beside it: A[2], Y[1], A[0], M
  // mux_2to1 mux_2to1_6: pin names not known; wires that end beside it: A[6], Y[5], A[4], M
  // mux_2to1 mux_2to1_7: pin names not known; wires that end beside it: A[1], Y[0], Cin, M
  // mux_2to1 mux_2to1_8: pin names not known; wires that end beside it: A[5], Y[4], A[3], M
  // mux_2to1 mux_2to1_9: pin names not known; wires that end beside it: A[0], Cout, A[7], M
endmodule

module multiplier_4 (
  input  [3:0] B,
  input  [3:0] A,
  output [7:0] Y,
  output Overflow
);

  wire or_1_out, or_2_out;
  wire [2:0] and_2_out;
  wire [3:0] and_5_out, and_9_out, and_13_out;
  wire [3:1] ripple_adder_4_1_y, ripple_adder_4_2_y;
  wire [3:3] ripple_adder_4_1_cout, ripple_adder_4_2_cout;

  and and_1 (Y[0], A[0], B[0]);
  and and_2 (and_2_out[0], A[1], B[0]);
  and and_3 (and_2_out[1], A[2], B[0]);
  and and_4 (and_2_out[2], A[3], B[0]);
  and and_5 (and_5_out[0], A[0], B[1]);
  and and_6 (and_5_out[1], A[1], B[1]);
  and and_7 (and_5_out[2], A[2], B[1]);
  and and_8 (and_5_out[3], A[3], B[1]);
  ripple_adder_4 ripple_adder_4_1 (
    .A(and_5_out), .B({1'b0, and_2_out}), .Cin(1'b0), .Y({ripple_adder_4_1_y, Y[1]}),
    .Cout(ripple_adder_4_1_cout[3]));
  or or_1 (or_1_out, Y[4], Y[5]);
  or or_2 (or_2_out, or_1_out, Y[6]);
  or or_3 (Overflow, Y[7], or_2_out);
  and and_9 (and_9_out[0], A[0], B[2]);
  and and_10 (and_9_out[1], A[1], B[2]);
  and and_11 (and_9_out[2], A[2], B[2]);
  and and_12 (and_9_out[3], A[3], B[2]);
  ripple_adder_4 ripple_adder_4_2 (
    .A(and_9_out), .B({ripple_adder_4_1_cout[3], ripple_adder_4_1_y}), .Cin(1'b0),
    .Y({ripple_adder_4_2_y, Y[2]}), .Cout(ripple_adder_4_2_cout[3]));
  and and_13 (and_13_out[0], A[0], B[3]);
  ripple_adder_4 ripple_adder_4_3 (
    .A(and_13_out), .B({ripple_adder_4_2_cout[3], ripple_adder_4_2_y}), .Cin(1'b0), .Y(Y[6:3]), .Cout(Y[7]));
  and and_14 (and_13_out[1], A[1], B[3]);
  and and_15 (and_13_out[2], A[2], B[3]);
  and and_16 (and_13_out[3], A[3], B[3]);
endmodule
